# Fritzing sketch PCB Layout (saved by Fritzing 1.0.3b)
circuit board: 7cm x 8cm
breadboards: 1

parts:
  BME280 = GY-BMP280 Breakout
  MPU9250 = gy9250
  XBEE_PRO = XBee Pro RF module
  BMP180 = Barometric Pressure Sensor - BMP180 Breakout (GY-68)
  Mod1 = Raspberry Pi Pico

nets:
  VCC: BME280.Pin_1, MPU9250.pin1, XBEE_PRO.VCC, BMP180.VCC, Mod1.pin_36
  GND: BME280.Pin_2, MPU9250.pin2, XBEE_PRO.GND, BMP180.GND, Mod1.pin_3, Mod1.pin_8, Mod1.pin_13, Mod1.pin_18, Mod1.pin_23, Mod1.pin_28, Mod1.pin_33, Mod1.pin_38, Mod1.pin_42
  N1: BME280.Pin_3, MPU9250.pin3, MPU9250.pin6, BMP180.SCL, Mod1.pin_2
  N2: BME280.Pin_4, MPU9250.pin4, MPU9250.pin5, BMP180.SDA, Mod1.pin_1
  N3: XBEE_PRO.DOUT, Mod1.pin_17
  N4: XBEE_PRO.DIN, Mod1.pin_16

custom parts:
  gy9250: MPU-9250 module (three-axis gyroscope + three-axis acceleration + three-axis magnetic field). The generic model from ebay et. al. rather than the Sparkfun version.
  Raspberry Pi Pico: Raspberry Pi Pico. Based around the RP2040 microcontroller the Pico is a low cost microcontroller device bringing Raspberry Pi quality, cost, and easy of use to the microcontroller space. Jan 2021, Split part in to two versions: tht (this one) and SMD. This one will drill holes for a .1 in header in pcb to allow plugging in the module as well as providing pads to solder the module to the top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
